# Fritzing sketch Schema logica (saved by Fritzing 1.0.6)
breadboards: 1

parts:
  U1 = ESP8266 ESP-01 Upgraded WiFi Module [part_number=ESP8266]
  Part1 = Arduino Uno (Rev3) - ICSP

nets:
  N1: U1.RXD, Part1.D0/RX
  VCC: U1.VCC, U1.CH_PD, Part1.3V3
  N2: U1.RST/GPIO_16, Part1.RESET
  GND: U1.GND, Part1.GND
  N3: U1.TXD, Part1.D1/TX

notes:
  ESP-01 are doua moduri cand GPIO0 e conectat intra in modul de programare cand e deconectat intra in modul de rulare program

custom parts:
  ESP8266 ESP-01 Upgraded WiFi Module: Upgraded Version ESP-01,all Flash are upgraded to 1M byte.Also support Cloud service remote transmission.
